// Logisim project basic.circ as structural Verilog: 14 circuits, main circuit mNot
module mNot (
  input  i,
  output o
);

  nand nand_1 (o, i, i);
endmodule

module mAnd (
  input  a,
  input  b,
  output o
);

  wire nand_1_out;

  nand nand_1 (nand_1_out, a, b);
  not not_1 (o, nand_1_out);
endmodule

module mOr (
  input  a,
  input  b,
  output o
);

  wire not_1_out, not_2_out;

  not not_1 (not_1_out, a);
  not not_2 (not_2_out, b);
  nand nand_1 (o, not_1_out, not_2_out);
endmodule

// Xor
module mXor (
  input  a,
  input  b,
  output o
);

  wire nand_1_out, nand_2_out, nand_3_out;

  nand nand_1 (nand_1_out, a, b);
  nand nand_2 (nand_2_out, a, nand_1_out);
  nand nand_3 (nand_3_out, nand_1_out, b);
  nand nand_4 (o, nand_2_out, nand_3_out);
endmodule

module Mux (
  input  a,
  input  b,
  input  sel,
  output o
);

  wire nand_1_out, nand_2_out, not_1_out;

  not not_1 (not_1_out, sel);
  nand nand_1 (nand_1_out, not_1_out, a);
  nand nand_2 (nand_2_out, b, sel);
  nand nand_3 (o, nand_1_out, nand_2_out);
endmodule

module DMux (
  input  i,
  input  sel,
  output a,
  output b
);

  wire nand_1_out, nand_2_out, not_1_out;

  not not_1 (not_1_out, sel);
  nand nand_1 (nand_1_out, i, not_1_out);
  not not_2 (a, nand_1_out);
  nand nand_2 (nand_2_out, sel, i);
  not not_3 (b, nand_2_out);
endmodule

module Not16 (
  input  [15:0] i,
  output [15:0] o
);

  assign o = ~i;  // NOT_Gate not_1, 16 bits wide
endmodule

module And16 (
  input  [15:0] a,
  input  [15:0] b,
  output [15:0] o
);

  assign o = a & b;  // AND_Gate and_1, 16 bits wide
endmodule

module Or8Way (
  input  [7:0] i,
  output o
);

  wire or_1_out, or_2_out, or_3_out, or_4_out, or_5_out, or_6_out;

  or or_1 (or_1_out, i[0], i[1]);
  or or_2 (or_2_out, i[2], i[3]);
  or or_3 (or_3_out, i[4], i[5]);
  or or_4 (or_4_out, i[6], i[7]);
  or or_5 (or_5_out, or_1_out, or_2_out);
  or or_6 (or_6_out, or_3_out, or_4_out);
  or or_7 (o, or_5_out, or_6_out);
endmodule

module mAnd16 (
  input  [15:0] a,
  input  [15:0] b,
  output [15:0] o
);

  and and_1 (o[0], a[0], b[0]);
  and and_2 (o[1], a[1], b[1]);
  and and_3 (o[2], a[2], b[2]);
  and and_4 (o[3], a[3], b[3]);
  and and_5 (o[4], a[4], b[4]);
  and and_6 (o[5], a[5], b[5]);
  and and_7 (o[6], a[6], b[6]);
  and and_8 (o[7], a[7], b[7]);
  and and_9 (o[8], a[8], b[8]);
  and and_10 (o[9], a[9], b[9]);
  and and_11 (o[10], a[10], b[10]);
  and and_12 (o[11], a[11], b[11]);
  and and_13 (o[12], a[12], b[12]);
  and and_14 (o[13], a[13], b[13]);
  and and_15 (o[14], a[14], b[14]);
  and and_16 (o[15], a[15], b[15]);
endmodule

module Mux16 (
  input  [15:0] a,
  input  [15:0] b,
  input  sel,
  output [15:0] o
);

  Mux mux_1 (.a(a[0]), .b(b[0]), .sel(sel), .o(o[0]));
  Mux mux_2 (.a(a[1]), .b(b[1]), .sel(sel), .o(o[1]));
  Mux mux_3 (.a(a[2]), .b(b[2]), .sel(sel), .o(o[2]));
  Mux mux_4 (.a(a[3]), .b(b[3]), .sel(sel), .o(o[3]));
  Mux mux_5 (.a(a[4]), .b(b[4]), .sel(sel), .o(o[4]));
  Mux mux_6 (.a(a[5]), .b(b[5]), .sel(sel), .o(o[5]));
  Mux mux_7 (.a(a[6]), .b(b[6]), .sel(sel), .o(o[6]));
  Mux mux_8 (.a(a[7]), .b(b[7]), .sel(sel), .o(o[7]));
  Mux mux_9 (.a(a[8]), .b(b[8]), .sel(sel), .o(o[8]));
  Mux mux_10 (.a(a[9]), .b(b[9]), .sel(sel), .o(o[9]));
  Mux mux_11 (.a(a[10]), .b(b[10]), .sel(sel), .o(o[10]));
  Mux mux_12 (.a(a[11]), .b(b[11]), .sel(sel), .o(o[11]));
  Mux mux_13 (.a(a[12]), .b(b[12]), .sel(sel), .o(o[12]));
  Mux mux_14 (.a(a[13]), .b(b[13]), .sel(sel), .o(o[13]));
  Mux mux_15 (.a(a[14]), .b(b[14]), .sel(sel), .o(o[14]));
  Mux mux_16 (.a(a[15]), .b(b[15]), .sel(sel), .o(o[15]));
endmodule

module And4Way (
  input  [3:0] i,
  output o
);

  wire and_1_out, and_2_out;

  and and_1 (and_1_out, i[0], i[1]);
  and and_2 (and_2_out, i[2], i[3]);
  and and_3 (o, and_1_out, and_2_out);
endmodule

module DMux8Way (
  input  i,
  input  [2:0] sel,
  output a,
  output b,
  output c,
  output d,
  output e,
  output f,
  output g,
  output h
);

  wire dmux_1_a, dmux_1_b, dmux_2_a, dmux_2_b, dmux_3_a, dmux_3_b;

  DMux dmux_1 (.i(i), .sel(sel[2]), .a(dmux_1_a), .b(dmux_1_b));
  DMux dmux_2 (.i(dmux_1_a), .sel(sel[1]), .a(dmux_2_a), .b(dmux_2_b));
  DMux dmux_3 (.i(dmux_1_b), .sel(sel[1]), .a(dmux_3_a), .b(dmux_3_b));
  DMux dmux_4 (.i(dmux_2_a), .sel(sel[0]), .a(a), .b(b));
  DMux dmux_5 (.i(dmux_2_b), .sel(sel[0]), .a(c), .b(d));
  DMux dmux_6 (.i(dmux_3_a), .sel(sel[0]), .a(e), .b(f));
  DMux dmux_7 (.i(dmux_3_b), .sel(sel[0]), .a(g), .b(h));
endmodule

module Mux8Way16 (
  input  [15:0] a,
  input  [15:0] b,
  input  [15:0] c,
  input  [15:0] d,
  input  [15:0] e,
  input  [15:0] f,
  input  [15:0] g,
  input  [15:0] h,
  input  [2:0] sel,
  output [15:0] o
);

  wire [15:0] mux16_1_o, mux16_2_o, mux16_3_o, mux16_4_o, mux16_5_o, mux16_6_o;

  Mux16 mux16_1 (.a(a), .b(b), .sel(sel[0]), .o(mux16_1_o));
  Mux16 mux16_2 (.a(c), .b(d), .sel(sel[0]), .o(mux16_2_o));
  Mux16 mux16_3 (.a(e), .b(f), .sel(sel[0]), .o(mux16_3_o));
  Mux16 mux16_4 (.a(g), .b(h), .sel(sel[0]), .o(mux16_4_o));
  Mux16 mux16_5 (.a(mux16_1_o), .b(mux16_2_o), .sel(sel[1]), .o(mux16_5_o));
  Mux16 mux16_6 (.a(mux16_3_o), .b(mux16_4_o), .sel(sel[1]), .o(mux16_6_o));
  Mux16 mux16_7 (.a(mux16_5_o), .b(mux16_6_o), .sel(sel[2]), .o(o));
endmodule
